// Logisim project alu.circ as structural Verilog: 1 circuit, main circuit alu
module alu (
  input  [31:0] A,
  input  [31:0] B,
  input  [3:0] ALUSel,
  output [31:0] ALUResult,
  output [31:0] out_5
);

  wire comparator_1_eq, comparator_1_gt, comparator_2_eq, comparator_2_gt, comparator_3_lt, or_1_out,
       or_2_out;
  wire [31:0] add0, and7, mul8, mulh9, mulhu11, or6, slt2, sra13, srl5, sub12, unused, xor4;

  Comparator #(.width(32)) comparator_1 (.a(B), .b(32'h20), .gt(comparator_1_gt), .eq(comparator_1_eq));  // open: lt
  Comparator #(.width(32)) comparator_2 (.a(B), .b(32'h20), .gt(comparator_2_gt), .eq(comparator_2_eq));  // open: lt
  Adder #(.width(32)) adder_1 (.a(A), .b(B), .out(add0));  // open: cin, cout
  Shifter #(.width(32)) shifter_1 (.in(A), .\dist (B[4:0]), .out(out_5));
  or or_1 (or_1_out, comparator_1_gt, comparator_1_eq);
  Comparator #(.width(32)) comparator_3 (.a(A), .b(B), .lt(comparator_3_lt));  // open: gt, eq
  assign xor4 = A ^ B;  // XOR_Gate xor_1, 32 bits wide
  Shifter #(.shift("lr"), .width(32)) shifter_2 (.in(A), .\dist (B[4:0]), .out(srl5));
  or or_2 (or_2_out, comparator_2_gt, comparator_2_eq);
  assign or6 = A | B;  // OR_Gate or_3, 32 bits wide
  assign and7 = A & B;  // AND_Gate and_1, 32 bits wide
  Multiplier #(.mode("twosComplement"), .width(32)) multiplier_1 (.a(A), .b(B), .out(mul8), .cout(mulh9));  // open: cin
  Multiplier #(.width(32)) multiplier_2 (.a(A), .b(B), .cout(mulhu11));  // open: out, cin
  Subtractor #(.width(32)) subtractor_1 (.a(A), .b(B), .out(sub12));  // open: bin, bout
  Shifter #(.shift("ar"), .width(32)) shifter_3 (.in(A), .\dist (B[4:0]), .out(sra13));
  Multiplexer #(.width(32)) multiplexer_1 (.in0({32{1'b0}}), .in1(32'h1), .out(slt2), .sel(comparator_3_lt));
  // Probe on ALUResult
  Multiplexer #(.select(4), .width(32)) multiplexer_2 (
    .in0(add0), .in1(out_5), .in2(slt2), .in3(unused), .in4(xor4), .in5(srl5), .in6(or6), .in7(and7),
    .in8(mul8), .in9(mulh9), .in10(unused), .in11(mulhu11), .in12(sub12), .in13(sra13), .in14(unused),
    .in15(B), .out(ALUResult), .sel(ALUSel));

  // Other names for the same wires on the sheet: bsel15[31:0] = B; sll1[31:0] = out_5

  // Notes on the sheet:
  //   INPUTS to your circuit
  //   DON'T CHANGE THE LOCATIONS OF THE INPUTS AND OUTPUTS!
  //   OUTPUT from your circuit
endmodule
