// Logisim project control-logic.circ as structural Verilog: 1 circuit, main circuit control_logic
module control_logic (
  input  [31:0] Instruction,
  input  BrEq,
  input  BrLt,
  output PCSel,
  output RegWEn,
  output [2:0] ImmSel,
  output BrUn,
  output ASel,
  output BSel,
  output [3:0] ALUSel,
  output MemWEn,
  output [1:0] WBSel
);

  wire add0, addi0, and11, and_9_out, and_10_out, and_11_out, and_12_out, and_13_out, and_14_out, and_15_out,
       and_16_out, and_17_out, and_18_out, and_19_out, and_20_out, and_21_out, andi7, auipc32, beq0, bge5,
       bgeu7, blt4, bltu6, bne1, Btype, comparator_2_eq, comparator_3_eq, comparator_4_eq, comparator_6_eq,
       comparator_7_eq, comparator_8_eq, comparator_9_eq, comparator_10_eq, comparator_11_eq,
       comparator_12_eq, comparator_13_eq, comparator_16_eq, comparator_17_eq, comparator_18_eq,
       comparator_19_eq, comparator_20_eq, comparator_21_eq, comparator_22_eq, comparator_23_eq,
       comparator_24_eq, comparator_25_eq, comparator_26_eq, comparator_27_eq, Ioadtype, Itype, jal34,
       jalr35, lb12, lh13, lui33, lw14, mul1, mulh4, mulhu5, not_1_out, not_2_out, not_3_out, or10, ori6,
       Rtype, sb23, sh24, sll3, slli1, slt6, slti2, sra9, srai, srasrli5, srl8, srli, Stype, sub2, sw25,
       xor7, xori4;
  wire [5:0] InstructionSel;
  wire [15:14] rom_1_data;

  Comparator #(.width(7)) comparator_1 (.a(Instruction[6:0]), .b(7'b0000011), .eq(Ioadtype));  // open: gt, lt
  Comparator #(.width(3)) comparator_2 (.a(Instruction[14:12]), .b(3'b000), .eq(comparator_2_eq));  // open: gt, lt
  Comparator #(.width(3)) comparator_3 (.a(Instruction[14:12]), .b(3'b001), .eq(comparator_3_eq));  // open: gt, lt
  Comparator #(.width(3)) comparator_4 (.a(Instruction[14:12]), .b(3'b010), .eq(comparator_4_eq));  // open: gt, lt
  Comparator #(.width(7)) comparator_5 (.a(Instruction[6:0]), .b(7'b0110011), .eq(Rtype));  // open: gt, lt
  Comparator #(.width(3)) comparator_6 (.a(Instruction[14:12]), .b(3'b000), .eq(comparator_6_eq));  // open: gt, lt
  Comparator #(.width(3)) comparator_7 (.a(Instruction[14:12]), .b(3'b001), .eq(comparator_7_eq));  // open: gt, lt
  Comparator #(.width(3)) comparator_8 (.a(Instruction[14:12]), .b(3'b011), .eq(comparator_8_eq));  // open: gt, lt
  Comparator #(.width(3)) comparator_9 (.a(Instruction[14:12]), .b(3'b010), .eq(comparator_9_eq));  // open: gt, lt
  Comparator #(.width(3)) comparator_10 (.a(Instruction[14:12]), .b(3'b100), .eq(comparator_10_eq));  // open: gt, lt
  Comparator #(.width(3)) comparator_11 (.a(Instruction[14:12]), .b(3'b101), .eq(comparator_11_eq));  // open: gt, lt
  Comparator #(.width(3)) comparator_12 (.a(Instruction[14:12]), .b(3'b110), .eq(comparator_12_eq));  // open: gt, lt
  Comparator #(.width(3)) comparator_13 (.a(Instruction[14:12]), .b(3'b111), .eq(comparator_13_eq));  // open: gt, lt
  Comparator #(.width(7)) comparator_14 (.a(Instruction[6:0]), .b(7'b0010011), .eq(Itype));  // open: gt, lt
  Comparator #(.width(7)) comparator_15 (.a(Instruction[6:0]), .b(7'b1100011), .eq(Btype));  // open: gt, lt
  ROM #(.addrWidth(6), .dataWidth(16)) rom_1 (
    .addr(InstructionSel), .data({rom_1_data, WBSel, MemWEn, ALUSel, BSel, ASel, BrUn, ImmSel, RegWEn}));
  and and_1 (lb12, Ioadtype, comparator_2_eq);
  and and_2 (lh13, Ioadtype, comparator_3_eq);
  and and_3 (lw14, Ioadtype, comparator_4_eq);
  not not_1 (not_1_out, BrEq);
  not not_2 (not_2_out, BrLt);
  not not_3 (not_3_out, BrLt);
  Comparator #(.width(7)) comparator_16 (.a(Instruction[31:25]), .b({7{1'b0}}), .eq(comparator_16_eq));  // open: gt, lt
  Comparator #(.width(7)) comparator_17 (
    .a(Instruction[31:25]), .b(7'b0000001), .eq(comparator_17_eq));  // open: gt, lt
  Comparator #(.width(7)) comparator_18 (
    .a(Instruction[31:25]), .b(7'b0100000), .eq(comparator_18_eq));  // open: gt, lt
  Comparator #(.width(7)) comparator_19 (.a(Instruction[31:25]), .b({7{1'b0}}), .eq(comparator_19_eq));  // open: gt, lt
  Comparator #(.width(7)) comparator_20 (
    .a(Instruction[31:25]), .b(7'b0000001), .eq(comparator_20_eq));  // open: gt, lt
  and and_4 (mulhu5, comparator_8_eq, Rtype);
  and and_5 (slt6, comparator_9_eq, Rtype);
  and and_6 (xor7, comparator_10_eq, Rtype);
  Comparator #(.width(7)) comparator_21 (.a(Instruction[31:25]), .b({7{1'b0}}), .eq(comparator_21_eq));  // open: gt, lt
  Comparator #(.width(7)) comparator_22 (
    .a(Instruction[31:25]), .b(7'b0100000), .eq(comparator_22_eq));  // open: gt, lt
  and and_7 (or10, comparator_12_eq, Rtype);
  and and_8 (and11, comparator_13_eq, Rtype);
  Decoder #(.select(3)) decoder_1 (
    .out0(addi0), .out1(slli1), .out2(slti2), .out4(xori4), .out5(srasrli5), .out6(ori6), .out7(andi7),
    .sel(Instruction[14:12]), .en(Itype));  // open: out3
  Comparator #(.width(7)) comparator_23 (.a(Instruction[31:25]), .b({7{1'b0}}), .eq(comparator_23_eq));  // open: gt, lt
  Comparator #(.width(7)) comparator_24 (
    .a(Instruction[31:25]), .b(7'b0100000), .eq(comparator_24_eq));  // open: gt, lt
  Decoder #(.select(3)) decoder_2 (
    .out0(beq0), .out1(bne1), .out4(blt4), .out5(bge5), .out6(bltu6), .out7(bgeu7), .sel(Instruction[14:12]),
    .en(Btype));  // open: out2, out3
  and and_9 (and_9_out, beq0, BrEq);
  and and_10 (and_10_out, bne1, not_1_out);
  and and_11 (and_11_out, blt4, BrLt);
  and and_12 (and_12_out, bge5, not_2_out);
  and and_13 (and_13_out, bltu6, BrLt);
  and and_14 (and_14_out, bgeu7, not_3_out);
  and and_15 (and_15_out, comparator_6_eq, comparator_16_eq);
  and and_16 (and_16_out, comparator_6_eq, comparator_17_eq);
  and and_17 (and_17_out, comparator_6_eq, comparator_18_eq);
  and and_18 (and_18_out, comparator_7_eq, comparator_19_eq);
  and and_19 (and_19_out, comparator_7_eq, comparator_20_eq);
  and and_20 (and_20_out, comparator_11_eq, comparator_21_eq);
  and and_21 (and_21_out, comparator_11_eq, comparator_22_eq);
  and and_22 (srli, srasrli5, comparator_23_eq);
  and and_23 (srai, srasrli5, comparator_24_eq);
  and and_24 (add0, and_15_out, Rtype);
  and and_25 (mul1, and_16_out, Rtype);
  and and_26 (sub2, and_17_out, Rtype);
  and and_27 (sll3, and_18_out, Rtype);
  and and_28 (mulh4, and_19_out, Rtype);
  and and_29 (srl8, and_20_out, Rtype);
  and and_30 (sra9, and_21_out, Rtype);
  // Probe on WBSel
  or or_1 (PCSel, and_9_out, and_10_out, and_11_out, and_12_out, and_13_out, and_14_out, jal34, jalr35);
  // Probe on InstructionSel
  // Priority_Encoder #(.select_enc(6)) priority_encoder_1: pin names not known; wires that end beside it: InstructionSel, add0, mul1, sub2, sll3, mulh4, mulhu5, slt6, xor7, srl8, sra9, or10, and11, lb12, lh13, lw14, addi0, slli1, slti2, xori4, srli, srai, ori6, andi7, sb23, sh24, sw25, beq0, bne1, blt4, bge5, bltu6, bgeu7, auipc32, lui33, jal34, jalr35
  Comparator #(.width(3)) comparator_25 (.a(Instruction[14:12]), .b(3'b000), .eq(comparator_25_eq));  // open: gt, lt
  Comparator #(.width(3)) comparator_26 (.a(Instruction[14:12]), .b(3'b001), .eq(comparator_26_eq));  // open: gt, lt
  Comparator #(.width(3)) comparator_27 (.a(Instruction[14:12]), .b(3'b010), .eq(comparator_27_eq));  // open: gt, lt
  Comparator #(.width(7)) comparator_28 (.a(Instruction[6:0]), .b(7'b0100011), .eq(Stype));  // open: gt, lt
  Comparator #(.width(7)) comparator_29 (.a(Instruction[6:0]), .b(7'b0110111), .eq(lui33));  // open: gt, lt
  Comparator #(.width(7)) comparator_30 (.a(Instruction[6:0]), .b(7'b0010111), .eq(auipc32));  // open: gt, lt
  Comparator #(.width(7)) comparator_31 (.a(Instruction[6:0]), .b(7'b1101111), .eq(jal34));  // open: gt, lt
  Comparator #(.width(7)) comparator_32 (.a(Instruction[6:0]), .b(7'b1100111), .eq(jalr35));  // open: gt, lt
  and and_31 (sb23, Stype, comparator_25_eq);
  and and_32 (sh24, Stype, comparator_26_eq);
  and and_33 (sw25, Stype, comparator_27_eq);

  // Other names for the same wires on the sheet: opcode[6:0] = Instruction[6:0]; rd[4:0] = Instruction[11:7];
  //   fun3[2:0] = Instruction[14:12]; rs1[4:0] = Instruction[19:15]; imm12[11:0] = Instruction[31:20];
  //   rs2[4:0] = Instruction[24:20]; fun7[6:0] = Instruction[31:25]

  // Notes on the sheet:
  //   INPUTS to your circuit
  //   Connect ROM Input here ->
  //   contents of rom_1 (hex, n*v repeats v):
  //   1001 1401 1601 1081 1481 1581 1101 1201 1281 1681 1301 1381 41 41 41 1041 10c1 1141 1241 12c1 16cb
  //   1341 13c1 842 842 842 4*1064 1074 1074 1067 3047 2069 2041
  //   ROM FOR CONTROL LOGIC
  //   DON'T CHANGE THE LOCATIONS OF THE INPUTS AND OUTPUTS!
  //   This is only if you choose to do the ROM option
  //   CONNECT
  //   WIRE
  //   TO
  //   USE
  //   ROM
  //   OUTPUT from your circuit
  //   Reminder: If using ROM, use combinational logic for PCSel
endmodule
