// Logisim project imm-gen.circ as structural Verilog: 1 circuit, main circuit imm_gen
module imm_gen (
  input  [31:0] Instruction,
  input  [2:0] ImmSel,
  output [31:0] Immediate
);

  wire [31:0] bit_extender_3_out, ImmBtype010, ImmItype000, ImmJtype100, ImmRtype101, ImmStype001,
       ImmUtype011;

  assign ImmItype000 = {{20{Instruction[31]}}, Instruction[31:20]};  // Bit_Extender bit_extender_1
  assign ImmStype001 = {{20{Instruction[31]}}, {Instruction[31:25], Instruction[11:7]}};  // Bit_Extender bit_extender_2
  assign bit_extender_3_out = {{12{Instruction[31]}}, Instruction[31:12]};  // Bit_Extender bit_extender_3
  assign ImmRtype101 = {{27{Instruction[24]}}, Instruction[24:20]};  // Bit_Extender bit_extender_4
  assign ImmBtype010 = {{19{Instruction[31]}}, {Instruction[31], Instruction[7], Instruction[30:25], Instruction[11:8], 1'b0}};  // Bit_Extender bit_extender_5
  Shifter #(.width(32)) shifter_1 (.in(bit_extender_3_out), .\dist (5'b01100), .out(ImmUtype011));
  assign ImmJtype100 = {{11{Instruction[31]}}, {Instruction[31], Instruction[19:12], Instruction[20], Instruction[30:21], 1'b0}};  // Bit_Extender bit_extender_6
  Multiplexer #(.select(3), .width(32)) multiplexer_1 (
    .in0(ImmItype000), .in1(ImmStype001), .in2(ImmBtype010), .in3(ImmUtype011), .in4(ImmJtype100),
    .in5(ImmRtype101), .out(Immediate), .sel(ImmSel));  // open: in6, in7

  // Notes on the sheet:
  //   INPUTS to your circuit
  //   DON'T CHANGE THE LOCATIONS OF THE INPUTS AND OUTPUTS!
  //   OUTPUT from your circuit
endmodule
